# Fritzing sketch circuit (saved by Fritzing 0.9.3b)
breadboards: 1

parts:
  パーツ1 = Arduino Uno (Rev3)
  Capacitive_Soil_Moisture_Sensor1 = DFRobot Capacitive Soil Moisture Sensor V1.0 [part_number=SEN0193]
  Capacitive_Soil_Moisture_Sensor2 = DFRobot Capacitive Soil Moisture Sensor V1.0 [part_number=SEN0193]

nets:
  N1: パーツ1.A0, Capacitive_Soil_Moisture_Sensor2.VCC
  N2: パーツ1.A1, Capacitive_Soil_Moisture_Sensor1.VCC
  GND: パーツ1.GND, Capacitive_Soil_Moisture_Sensor1.GND, Capacitive_Soil_Moisture_Sensor2.GND
  N3: パーツ1.D0/RX, Capacitive_Soil_Moisture_Sensor1.A
  N4: パーツ1.D1/TX, Capacitive_Soil_Moisture_Sensor2.A

custom parts:
  DFRobot Capacitive Soil Moisture Sensor V1.0: DFRobot Capacitive Soil Moisture Sensor V1.0 This product measures soil moisture levels by capacitive sensing, rather than resistive sensing like other types of moisture sensor. It is made of a corrosion resistant material giving it a long service life. Insert it into soil and impress your friends with the real-time soil moisture data! The product includes an on-board voltage regulator which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
